# Fritzing sketch p2_fritzing (saved by Fritzing 0.9.2b)
breadboards: 1

parts:
  Part1 = Arduino Uno (Rev3)
  U1 = BATTERY-2 [package=battery-aa]
  U2 = BATTERY-2 [package=battery-aa]
  U3 = BATTERY-2 [package=battery-aa]
  U4 = BATTERY-2 [package=battery-aa]
  U5 = BATTERY-2 [package=battery-aa]
  U6 = BATTERY-2 [package=battery-aa]
  NEOPIXEL32 = Neopixel Strip -- Black (60/m)  # not connected
  NEOPIXEL7 = Neopixel Strip -- Black (60/m)
  NEOPIXEL14 = Neopixel Strip -- Black (60/m)  # not connected
  NEOPIXEL3 = Neopixel Strip -- Black (60/m)
  NEOPIXEL4 = Neopixel Strip -- Black (60/m)
  NEOPIXEL31 = Neopixel Strip -- Black (60/m)  # not connected
  NEOPIXEL10 = Neopixel Strip -- Black (60/m)  # not connected
  NEOPIXEL11 = Neopixel Strip -- Black (60/m)  # not connected
  C1 = Electrolytic Capacitor [capacitance=220µF package="100 mil [THT, electrolytic]"]
  R1 = Resistor [tolerance=±5% resistance=510 package=THT]
  C3 = Electrolytic Capacitor [capacitance=1µF package="100 mil [THT, electrolytic]"]
  C4 = Electrolytic Capacitor [capacitance=1µF package="100 mil [THT, electrolytic]"]
  NEOPIXEL35 = Neopixel Strip -- Black (60/m)
  NEOPIXEL36 = Neopixel Strip -- Black (60/m)  # not connected
  NEOPIXEL38 = Neopixel Strip -- Black (60/m)
  NEOPIXEL37 = Neopixel Strip -- Black (60/m)
  NEOPIXEL39 = Neopixel Strip -- Black (60/m)
  NEOPIXEL40 = Neopixel Strip -- Black (60/m)  # not connected
  NEOPIXEL41 = Neopixel Strip -- Black (60/m)
  NEOPIXEL42 = Neopixel Strip -- Black (60/m)
  NEOPIXEL43 = Neopixel Strip -- Black (60/m)
  NEOPIXEL44 = Neopixel Strip -- Black (60/m)
  NEOPIXEL45 = Neopixel Strip -- Black (60/m)
  NEOPIXEL46 = Neopixel Strip -- Black (60/m)
  NEOPIXEL47 = Neopixel Strip -- Black (60/m)
  NEOPIXEL48 = Neopixel Strip -- Black (60/m)
  NEOPIXEL49 = Neopixel Strip -- Black (60/m)
  NEOPIXEL50 = Neopixel Strip -- Black (60/m)
  NEOPIXEL51 = Neopixel Strip -- Black (60/m)  # not connected
  NEOPIXEL52 = Neopixel Strip -- Black (60/m)
  NEOPIXEL53 = Neopixel Strip -- Black (60/m)
  NEOPIXEL54 = Neopixel Strip -- Black (60/m)
  NEOPIXEL55 = Neopixel Strip -- Black (60/m)
  NEOPIXEL56 = Neopixel Strip -- Black (60/m)
  NEOPIXEL57 = Neopixel Strip -- Black (60/m)
  NEOPIXEL58 = Neopixel Strip -- Black (60/m)
  NEOPIXEL59 = Neopixel Strip -- Black (60/m)
  NEOPIXEL60 = Neopixel Strip -- Black (60/m)
  NEOPIXEL61 = Neopixel Strip -- Black (60/m)  # not connected
  NEOPIXEL62 = Neopixel Strip -- Black (60/m)
  NEOPIXEL63 = Neopixel Strip -- Black (60/m)
  NEOPIXEL64 = Neopixel Strip -- Black (60/m)
  C5 = Electrolytic Capacitor [capacitance=1µF package="100 mil [THT, electrolytic]"]
  C6 = Electrolytic Capacitor [capacitance=1µF package="100 mil [THT, electrolytic]"]
  CC1 = Adafruit CC3000 Shield for Arduino

nets:
  N1: Part1.A0, CC1.A0
  N2: Part1.A1, CC1.A1
  N3: Part1.A2, CC1.A2
  N4: Part1.A3, CC1.A3
  N5: Part1.A4/SDA, CC1.A4
  N6: Part1.A5/SCL, CC1.A5
  GND: Part1.GND, U1.-1, U4.-1, NEOPIXEL3.GND, C1.+, C3.+, C4.+, C5.+, C6.+, CC1.GND
  N7: Part1.D0/RX, CC1.D0
  N8: Part1.D1/TX, CC1.D1
  N9: Part1.D2, R1.Pin_0, CC1.D2
  N10: Part1.D3_PWM, CC1.D3
  N11: Part1.D4, CC1.D4
  N12: Part1.D5_PWM, CC1.D5
  N13: Part1.D6_PWM, CC1.D6
  N14: Part1.D7, CC1.D7
  N15: Part1.ioref, CC1.IOr
  N16: Part1.RESET, CC1.RST
  N17: Part1.3V3, CC1.3V
  5V: Part1.5V, CC1.5V
  VIN: Part1.VIN, CC1.VIN
  N18: Part1.N/C, CC1.NC
  N19: U1.+1, U5.-1
  N20: U2.-1, U5.+1
  N21: U2.+1, U3.+1, NEOPIXEL3.DI, C1.-, C3.-, C4.-, C5.-, C6.-
  N22: U3.-1, U6.+1
  N23: U4.+1, U6.-1
  +5V: NEOPIXEL7.+5V, NEOPIXEL4.+5V, NEOPIXEL35.+5V
  N24: NEOPIXEL7.DI, NEOPIXEL4.DO, NEOPIXEL35.DI
  GND_2: NEOPIXEL7.GND, NEOPIXEL4.GND, NEOPIXEL35.GND
  N25: NEOPIXEL3.+5V, R1.Pin_1
  +5V_2: NEOPIXEL38.+5V, NEOPIXEL37.+5V, NEOPIXEL41.+5V, NEOPIXEL42.+5V
  N26: NEOPIXEL38.DI, NEOPIXEL37.DO, NEOPIXEL41.DI, NEOPIXEL42.DI
  GND_3: NEOPIXEL38.GND, NEOPIXEL37.GND, NEOPIXEL41.GND, NEOPIXEL42.GND
  +5V_3: NEOPIXEL39.+5V, NEOPIXEL43.+5V, NEOPIXEL45.+5V, NEOPIXEL46.+5V
  N27: NEOPIXEL39.DI, NEOPIXEL43.DO, NEOPIXEL45.DI, NEOPIXEL46.DO
  GND_4: NEOPIXEL39.GND, NEOPIXEL43.GND, NEOPIXEL45.GND, NEOPIXEL46.GND
  GND_5: NEOPIXEL44.GND, NEOPIXEL47.GND
  N28: NEOPIXEL44.DO, NEOPIXEL47.DI
  +5V_4: NEOPIXEL44.+5V, NEOPIXEL47.+5V
  +5V_5: NEOPIXEL48.+5V, NEOPIXEL52.+5V, NEOPIXEL55.+5V, NEOPIXEL60.+5V, NEOPIXEL62.+5V, NEOPIXEL63.+5V
  N29: NEOPIXEL48.DI, NEOPIXEL52.DO, NEOPIXEL55.DI, NEOPIXEL60.DI, NEOPIXEL62.DI, NEOPIXEL63.DO
  GND_6: NEOPIXEL48.GND, NEOPIXEL52.GND, NEOPIXEL55.GND, NEOPIXEL60.GND, NEOPIXEL62.GND, NEOPIXEL63.GND
  +5V_6: NEOPIXEL49.+5V, NEOPIXEL50.+5V, NEOPIXEL54.+5V
  N30: NEOPIXEL49.DI, NEOPIXEL50.DO, NEOPIXEL54.DI
  GND_7: NEOPIXEL49.GND, NEOPIXEL50.GND, NEOPIXEL54.GND
  GND_8: NEOPIXEL53.GND, NEOPIXEL56.GND, NEOPIXEL57.GND, NEOPIXEL58.GND, NEOPIXEL59.GND, NEOPIXEL64.GND
  N31: NEOPIXEL53.DO, NEOPIXEL56.DO, NEOPIXEL57.DI, NEOPIXEL58.DI, NEOPIXEL59.DO, NEOPIXEL64.DO
  +5V_7: NEOPIXEL53.+5V, NEOPIXEL56.+5V, NEOPIXEL57.+5V, NEOPIXEL58.+5V, NEOPIXEL59.+5V, NEOPIXEL64.+5V

notes:
  8x8 LED matrix
  Capacitor bank:
  1.1mF, 63 V
  Battery pack:
  4.5V, 5600mA

custom parts:
  Neopixel Strip -- Black (60/m): Neopixel Strip, Black, 60 pixels per meter.
